// Logisim project sketch_16x.circ as structural Verilog: 6 circuits, main circuit CPU
module CPU (
);

  wire clk, clr, jump, ldMem, strMem, strReg;
  wire [2:0] control_logic_1_p2;
  wire [3:0] rom_1_instruction, rom_1_instruction_2, rom_1_instruction_3, rom_1_instruction_4, undriven;
  wire [15:0] A, alu_1_dataout, D2, demultiplexer_1_out0, demultiplexer_1_out1, multiplexer_1_out,
       ram_1_dataout, regs_1_data1;

  ROM rom_1 (
    .Address(A),
    .Instruction({rom_1_instruction_4, rom_1_instruction_3, rom_1_instruction_2, rom_1_instruction}),
    .jump(jump), .clk(clk), .clr(clr));
  // Control_Logic control_logic_1: pin names not known; wires that end beside it: rom_1_instruction, control_logic_1_p2
  Regs regs_1 (
    .RegSelect(rom_1_instruction_3), .RegTelect(rom_1_instruction_4), .RedDest(rom_1_instruction_2),
    .DataIn(multiplexer_1_out), .Data1(regs_1_data1), .Data2(D2), .str(strReg), .clk(clk), .clr(clr));
  Demultiplexer #(.width(16)) demultiplexer_1 (
    .out0(demultiplexer_1_out0), .out1(demultiplexer_1_out1), .in(alu_1_dataout), .sel(ldMem));  // open: en
  ALU alu_1 (
    .Data1(regs_1_data1), .Data2(D2), .DataOut(alu_1_dataout), .ALUOp(control_logic_1_p2),
    .Immed({rom_1_instruction_4, rom_1_instruction_3, rom_1_instruction_2, undriven}));  // open: Zero
  Multiplexer #(.width(16)) multiplexer_1 (
    .in0(demultiplexer_1_out0), .in1(ram_1_dataout), .out(multiplexer_1_out), .sel(ldMem));  // open: en
  RAM ram_1 (
    .Address(demultiplexer_1_out1), .DataIn(D2), .DataOut(ram_1_dataout), .sw(strMem), .clk(clk), .lw(ldMem),
    .clr(clr));

  // Notes on the sheet:
  //   Data1
  //   Data2
  //   Immed
endmodule

// Ctrl
module Control_Logic (
  input  [3:0] operation,
  output out_2,
  output out_3,
  output out_4,
  output out_5,
  output out_6,
  output out_7,
  output [3:0] ALUop
);
endmodule

module ALU (
  input  [2:0] ALUOp,
  input  [15:0] Data1,
  input  [15:0] Data2,
  input  [15:0] Immed,
  output [15:0] DataOut,
  output Zero
);

  wire comparator_1_gt;
  wire [15:0] adder_1_out, adder_2_out, bit_extender_1_out, shifter_1_out, shifter_2_out, subtractor_1_out,
       subtractor_2_out;

  Adder #(.width(16)) adder_1 (.a(Data1), .b(Data2), .out(adder_1_out));  // open: cin, cout
  Adder #(.width(16)) adder_2 (.a(Data1), .b(Immed), .out(adder_2_out));  // open: cin, cout
  Subtractor #(.width(16)) subtractor_1 (.a(Data1), .b(Data2), .out(subtractor_1_out));  // open: bin, bout
  Subtractor #(.width(16)) subtractor_2 (.a(Data1), .b(Immed), .out(subtractor_2_out));  // open: bin, bout
  Shifter #(.width(16)) shifter_1 (.in(Data1), .\dist (Immed[15:12]), .out(shifter_1_out));
  Shifter #(.width(16), .shift("lr")) shifter_2 (.in(Data1), .\dist (Immed[15:12]), .out(shifter_2_out));
  assign bit_extender_1_out = {{15{1'b0}}, comparator_1_gt};  // Bit_Extender bit_extender_1
  Comparator #(.width(16)) comparator_1 (.a(Data1), .b(Data2), .gt(comparator_1_gt));  // open: eq, lt
  Multiplexer #(.select(3), .width(16)) multiplexer_1 (
    .in0(Immed), .in1(adder_1_out), .in2(adder_2_out), .in3(subtractor_1_out), .in4(subtractor_2_out),
    .in5(shifter_1_out), .in6(shifter_2_out), .in7(bit_extender_1_out), .out(DataOut), .sel(ALUOp));  // open: en
  and and_1 (Zero, DataOut[0], DataOut[1], DataOut[2], DataOut[3], DataOut[4], DataOut[5], DataOut[6], DataOut[7], DataOut[8], DataOut[9], DataOut[10], DataOut[11], DataOut[12], DataOut[13], DataOut[14], DataOut[15]);
endmodule

module Regs (
  input  str,
  input  [3:0] RegSelect,
  input  [3:0] RegTelect,
  input  [3:0] RedDest,
  input  [15:0] DataIn,
  input  clk,
  input  clr,
  output [15:0] Data1,
  output [15:0] Data2
);

  wire demultiplexer_1_out0, demultiplexer_1_out1, demultiplexer_1_out2, demultiplexer_1_out3,
       demultiplexer_1_out4, demultiplexer_1_out5, demultiplexer_1_out6, demultiplexer_1_out7,
       demultiplexer_1_out8, demultiplexer_1_out9, demultiplexer_1_out10, demultiplexer_1_out11,
       demultiplexer_1_out12, demultiplexer_1_out13, demultiplexer_1_out14, demultiplexer_1_out15;
  wire [15:0] demultiplexer_2_out0, demultiplexer_2_out1, demultiplexer_2_out2, demultiplexer_2_out3,
       demultiplexer_2_out4, demultiplexer_2_out5, demultiplexer_2_out6, demultiplexer_2_out7,
       demultiplexer_2_out8, demultiplexer_2_out9, demultiplexer_2_out10, demultiplexer_2_out11,
       demultiplexer_2_out12, demultiplexer_2_out13, demultiplexer_2_out14, demultiplexer_2_out15,
       register_1_q, register_2_q, register_3_q, register_4_q, register_5_q, register_6_q, register_7_q,
       register_8_q, register_9_q, register_10_q, register_11_q, register_12_q, register_13_q, register_14_q,
       register_15_q, register_16_q;

  Demultiplexer #(.select(4)) demultiplexer_1 (
    .out0(demultiplexer_1_out0), .out1(demultiplexer_1_out1), .out2(demultiplexer_1_out2),
    .out3(demultiplexer_1_out3), .out4(demultiplexer_1_out4), .out5(demultiplexer_1_out5),
    .out6(demultiplexer_1_out6), .out7(demultiplexer_1_out7), .out8(demultiplexer_1_out8),
    .out9(demultiplexer_1_out9), .out10(demultiplexer_1_out10), .out11(demultiplexer_1_out11),
    .out12(demultiplexer_1_out12), .out13(demultiplexer_1_out13), .out14(demultiplexer_1_out14),
    .out15(demultiplexer_1_out15), .in(str), .sel(RedDest));  // open: en
  Demultiplexer #(.select(4), .width(16)) demultiplexer_2 (
    .out0(demultiplexer_2_out0), .out1(demultiplexer_2_out1), .out2(demultiplexer_2_out2),
    .out3(demultiplexer_2_out3), .out4(demultiplexer_2_out4), .out5(demultiplexer_2_out5),
    .out6(demultiplexer_2_out6), .out7(demultiplexer_2_out7), .out8(demultiplexer_2_out8),
    .out9(demultiplexer_2_out9), .out10(demultiplexer_2_out10), .out11(demultiplexer_2_out11),
    .out12(demultiplexer_2_out12), .out13(demultiplexer_2_out13), .out14(demultiplexer_2_out14),
    .out15(demultiplexer_2_out15), .in(DataIn), .sel(RedDest));  // open: en
  Register #(.width(16)) register_1 (
    .D(demultiplexer_2_out0), .en(demultiplexer_1_out0), .Q(register_1_q), .clk(clk), .clr(clr));
  Register #(.width(16)) register_2 (
    .D(demultiplexer_2_out1), .en(demultiplexer_1_out1), .Q(register_2_q), .clk(clk), .clr(clr));
  Register #(.width(16)) register_3 (
    .D(demultiplexer_2_out2), .en(demultiplexer_1_out2), .Q(register_3_q), .clk(clk), .clr(clr));
  Register #(.width(16)) register_4 (
    .D(demultiplexer_2_out3), .en(demultiplexer_1_out3), .Q(register_4_q), .clk(clk), .clr(clr));
  Register #(.width(16)) register_5 (
    .D(demultiplexer_2_out4), .en(demultiplexer_1_out4), .Q(register_5_q), .clk(clk), .clr(clr));
  Register #(.width(16)) register_6 (
    .D(demultiplexer_2_out5), .en(demultiplexer_1_out5), .Q(register_6_q), .clk(clk), .clr(clr));
  Register #(.width(16)) register_7 (
    .D(demultiplexer_2_out6), .en(demultiplexer_1_out6), .Q(register_7_q), .clk(clk), .clr(clr));
  Register #(.width(16)) register_8 (
    .D(demultiplexer_2_out7), .en(demultiplexer_1_out7), .Q(register_8_q), .clk(clk), .clr(clr));
  Register #(.width(16)) register_9 (
    .D(demultiplexer_2_out8), .en(demultiplexer_1_out8), .Q(register_9_q), .clk(clk), .clr(clr));
  Register #(.width(16)) register_10 (
    .D(demultiplexer_2_out9), .en(demultiplexer_1_out9), .Q(register_10_q), .clk(clk), .clr(clr));
  Register #(.width(16)) register_11 (
    .D(demultiplexer_2_out10), .en(demultiplexer_1_out10), .Q(register_11_q), .clk(clk), .clr(clr));
  Register #(.width(16)) register_12 (
    .D(demultiplexer_2_out11), .en(demultiplexer_1_out11), .Q(register_12_q), .clk(clk), .clr(clr));
  Register #(.width(16)) register_13 (
    .D(demultiplexer_2_out12), .en(demultiplexer_1_out12), .Q(register_13_q), .clk(clk), .clr(clr));
  Register #(.width(16)) register_14 (
    .D(demultiplexer_2_out13), .en(demultiplexer_1_out13), .Q(register_14_q), .clk(clk), .clr(clr));
  Register #(.width(16)) register_15 (
    .D(demultiplexer_2_out14), .en(demultiplexer_1_out14), .Q(register_15_q), .clk(clk), .clr(clr));
  Register #(.width(16)) register_16 (
    .D(demultiplexer_2_out15), .en(demultiplexer_1_out15), .Q(register_16_q), .clk(clk), .clr(clr));
  Multiplexer #(.select(4), .width(16)) multiplexer_1 (
    .in0(register_1_q), .in1(register_2_q), .in2(register_3_q), .in3(register_4_q), .in4(register_5_q),
    .in5(register_6_q), .in6(register_7_q), .in7(register_8_q), .in8(register_9_q), .in9(register_10_q),
    .in10(register_11_q), .in11(register_12_q), .in12(register_13_q), .in13(register_14_q),
    .in14(register_15_q), .in15(register_16_q), .out(Data1), .sel(RegSelect));  // open: en
  Multiplexer #(.select(4), .width(16)) multiplexer_2 (
    .in0(register_1_q), .in1(register_2_q), .in2(register_3_q), .in3(register_4_q), .in4(register_5_q),
    .in5(register_6_q), .in6(register_7_q), .in7(register_8_q), .in8(register_9_q), .in9(register_10_q),
    .in10(register_11_q), .in11(register_12_q), .in12(register_13_q), .in13(register_14_q),
    .in14(register_15_q), .in15(register_16_q), .out(Data2), .sel(RegTelect));  // open: en

  // Other names for the same wires on the sheet: RS[3:0] = RegSelect; RT[3:0] = RegTelect
endmodule

module ROM (
  input  [15:0] Address,
  input  jump,
  input  clk,
  input  clr,
  output [15:0] Instruction
);

  wire [15:0] adder_1_out, multiplexer_1_out, PC_q;

  Multiplexer #(.width(16)) multiplexer_1 (
    .in0(adder_1_out), .in1(Address), .out(multiplexer_1_out), .sel(jump));  // open: en
  Register #(.width(16)) PC (.D(multiplexer_1_out), .Q(PC_q), .clk(clk), .clr(clr));  // open: en
  Adder #(.width(16)) adder_1 (.a(16'h1), .b(PC_q), .out(adder_1_out));  // open: cin, cout
  ROM_part #(.addrWidth(16), .dataWidth(16)) rom_1 (.addr(PC_q), .data(Instruction));  // open: sel

  // Notes on the sheet:
  //   contents of rom_1 (hex, n*v repeats v):
  //   111 0 44
endmodule

// MEM
module RAM (
  input  [15:0] Address,
  input  [15:0] DataIn,
  input  sw,
  input  clk,
  input  lw,
  input  clr,
  output [15:0] DataOut
);

  RAM_part #(.addrWidth(16), .dataWidth(16), .bus("separate")) ram_1 (
    .addr(Address), .din(DataIn), .data(DataOut), .str(sw), .sel(1'b1), .clk(clk), .ld(lw), .clr(clr));
endmodule
